// Logisim project ALU.circ as structural Verilog: 11 circuits, main circuit main
module main (
  input  [31:0] a,
  input  [31:0] b,
  input  [2:0] c,
  output [31:0] o
);

  wire [31:0] divider_1_out, l_32_bit_adder_cc387356_1_result, l_32_bit_and_28c7e6f7_1_result,
       l_32_bit_or_08d9d074_1_result, l_32_bit_subtractor_26bf78db_1_s, multiplier_1_out,
       not_32_bit_929ae11d_1_nota, two_s_complement_32_bit_72d07b45_1_twosompa;

  NOT_32_bit_929ae11d not_32_bit_929ae11d_1 (.A(a), .NotA(not_32_bit_929ae11d_1_nota));
  L_32_bit_OR_08d9d074 l_32_bit_or_08d9d074_1 (.A(b), .B(a), .Result(l_32_bit_or_08d9d074_1_result));
  L_32_bit_AND_28c7e6f7 l_32_bit_and_28c7e6f7_1 (.A(b), .B(a), .Result(l_32_bit_and_28c7e6f7_1_result));
  Two_s_Complement_32_bit_72d07b45 two_s_complement_32_bit_72d07b45_1 (
    .A(a), .TwosompA(two_s_complement_32_bit_72d07b45_1_twosompa));
  L_32_bit_Adder_cc387356 l_32_bit_adder_cc387356_1 (.A(a), .B(b), .Result(l_32_bit_adder_cc387356_1_result));
  L_32_bit_Subtractor_26bf78db l_32_bit_subtractor_26bf78db_1 (
    .A(a), .S(l_32_bit_subtractor_26bf78db_1_s), .B(b));  // open: OF, Cout
  Multiplier #(.width(32)) multiplier_1 (.a(a), .b(b), .out(multiplier_1_out));  // open: cin, cout
  Divider #(.width(32)) divider_1 (.a(a), .b(b), .out(divider_1_out));  // open: upper, rem
  Multiplexer #(.select(3), .width(32)) multiplexer_1 (
    .in0(not_32_bit_929ae11d_1_nota), .in1(l_32_bit_or_08d9d074_1_result),
    .in2(l_32_bit_and_28c7e6f7_1_result), .in3(two_s_complement_32_bit_72d07b45_1_twosompa),
    .in4(l_32_bit_adder_cc387356_1_result), .in5(l_32_bit_subtractor_26bf78db_1_s), .in6(multiplier_1_out),
    .in7(divider_1_out), .out(o), .sel(c));  // open: en

  // Notes on the sheet:
  //   Control bits:
  //   000: NOT Gate
  //   001: OR Gate
  //   010: AND Gate
  //   011: Negation
  //   100: ADDER
  //   101: Subtractor
  //   110: Multiplier
  //   111: Divisor
  //   Input1
  //   Input2
  //   NOT
  //   OR
  //   AND
  //   Negation
  //   ADD
  //   Subtract
  //   Multiplier
  //   Division
  //   Control bits
  //   Output
endmodule

module L_32_bit_Adder_cc387356 (
  input  [31:0] A,
  input  [31:0] B,
  output [31:0] Result
);

  wire full_adder_a5a39aab_1_carry_out_a019e228, full_adder_a5a39aab_2_carry_out_a019e228,
       full_adder_a5a39aab_3_carry_out_a019e228, full_adder_a5a39aab_4_carry_out_a019e228,
       full_adder_a5a39aab_5_carry_out_a019e228, full_adder_a5a39aab_6_carry_out_a019e228,
       full_adder_a5a39aab_7_carry_out_a019e228, full_adder_a5a39aab_8_carry_out_a019e228,
       full_adder_a5a39aab_9_carry_out_a019e228, full_adder_a5a39aab_10_carry_out_a019e228,
       full_adder_a5a39aab_11_carry_out_a019e228, full_adder_a5a39aab_12_carry_out_a019e228,
       full_adder_a5a39aab_13_carry_out_a019e228, full_adder_a5a39aab_14_carry_out_a019e228,
       full_adder_a5a39aab_15_carry_out_a019e228, full_adder_a5a39aab_16_carry_out_a019e228,
       full_adder_a5a39aab_17_carry_out_a019e228, full_adder_a5a39aab_18_carry_out_a019e228,
       full_adder_a5a39aab_19_carry_out_a019e228, full_adder_a5a39aab_20_carry_out_a019e228,
       full_adder_a5a39aab_21_carry_out_a019e228, full_adder_a5a39aab_22_carry_out_a019e228,
       full_adder_a5a39aab_23_carry_out_a019e228, full_adder_a5a39aab_24_carry_out_a019e228,
       full_adder_a5a39aab_25_carry_out_a019e228, full_adder_a5a39aab_26_carry_out_a019e228,
       full_adder_a5a39aab_27_carry_out_a019e228, full_adder_a5a39aab_28_carry_out_a019e228,
       full_adder_a5a39aab_29_carry_out_a019e228, full_adder_a5a39aab_30_carry_out_a019e228,
       full_adder_a5a39aab_31_carry_out_a019e228;

  Full_Adder_a5a39aab full_adder_a5a39aab_1 (
    .A(A[24]), .B(B[24]), .Carry_In_17b5218c(1'b0), .Result(Result[24]),
    .Carry_out_a019e228(full_adder_a5a39aab_1_carry_out_a019e228));
  Full_Adder_a5a39aab full_adder_a5a39aab_2 (
    .A(A[25]), .B(B[25]), .Carry_In_17b5218c(full_adder_a5a39aab_1_carry_out_a019e228), .Result(Result[25]),
    .Carry_out_a019e228(full_adder_a5a39aab_2_carry_out_a019e228));
  Full_Adder_a5a39aab full_adder_a5a39aab_3 (
    .A(A[26]), .B(B[26]), .Carry_In_17b5218c(full_adder_a5a39aab_2_carry_out_a019e228), .Result(Result[26]),
    .Carry_out_a019e228(full_adder_a5a39aab_3_carry_out_a019e228));
  Full_Adder_a5a39aab full_adder_a5a39aab_4 (
    .A(A[27]), .B(B[27]), .Carry_In_17b5218c(full_adder_a5a39aab_3_carry_out_a019e228), .Result(Result[27]),
    .Carry_out_a019e228(full_adder_a5a39aab_4_carry_out_a019e228));
  Full_Adder_a5a39aab full_adder_a5a39aab_5 (
    .A(A[28]), .B(B[28]), .Carry_In_17b5218c(full_adder_a5a39aab_4_carry_out_a019e228), .Result(Result[28]),
    .Carry_out_a019e228(full_adder_a5a39aab_5_carry_out_a019e228));
  Full_Adder_a5a39aab full_adder_a5a39aab_6 (
    .A(A[29]), .B(B[29]), .Carry_In_17b5218c(full_adder_a5a39aab_5_carry_out_a019e228), .Result(Result[29]),
    .Carry_out_a019e228(full_adder_a5a39aab_6_carry_out_a019e228));
  Full_Adder_a5a39aab full_adder_a5a39aab_7 (
    .A(A[30]), .B(B[30]), .Carry_In_17b5218c(full_adder_a5a39aab_6_carry_out_a019e228), .Result(Result[30]),
    .Carry_out_a019e228(full_adder_a5a39aab_7_carry_out_a019e228));
  Full_Adder_a5a39aab full_adder_a5a39aab_8 (
    .A(A[31]), .B(B[31]), .Carry_In_17b5218c(full_adder_a5a39aab_7_carry_out_a019e228), .Result(Result[31]),
    .Carry_out_a019e228(full_adder_a5a39aab_8_carry_out_a019e228));
  Full_Adder_a5a39aab full_adder_a5a39aab_9 (
    .A(A[16]), .B(B[16]), .Carry_In_17b5218c(full_adder_a5a39aab_8_carry_out_a019e228), .Result(Result[16]),
    .Carry_out_a019e228(full_adder_a5a39aab_9_carry_out_a019e228));
  Full_Adder_a5a39aab full_adder_a5a39aab_10 (
    .A(A[17]), .B(B[17]), .Carry_In_17b5218c(full_adder_a5a39aab_9_carry_out_a019e228), .Result(Result[17]),
    .Carry_out_a019e228(full_adder_a5a39aab_10_carry_out_a019e228));
  Full_Adder_a5a39aab full_adder_a5a39aab_11 (
    .A(A[18]), .B(B[18]), .Carry_In_17b5218c(full_adder_a5a39aab_10_carry_out_a019e228), .Result(Result[18]),
    .Carry_out_a019e228(full_adder_a5a39aab_11_carry_out_a019e228));
  Full_Adder_a5a39aab full_adder_a5a39aab_12 (
    .A(A[19]), .B(B[19]), .Carry_In_17b5218c(full_adder_a5a39aab_11_carry_out_a019e228), .Result(Result[19]),
    .Carry_out_a019e228(full_adder_a5a39aab_12_carry_out_a019e228));
  Full_Adder_a5a39aab full_adder_a5a39aab_13 (
    .A(A[20]), .B(B[20]), .Carry_In_17b5218c(full_adder_a5a39aab_12_carry_out_a019e228), .Result(Result[20]),
    .Carry_out_a019e228(full_adder_a5a39aab_13_carry_out_a019e228));
  Full_Adder_a5a39aab full_adder_a5a39aab_14 (
    .A(A[21]), .B(B[21]), .Carry_In_17b5218c(full_adder_a5a39aab_13_carry_out_a019e228), .Result(Result[21]),
    .Carry_out_a019e228(full_adder_a5a39aab_14_carry_out_a019e228));
  Full_Adder_a5a39aab full_adder_a5a39aab_15 (
    .A(A[22]), .B(B[22]), .Carry_In_17b5218c(full_adder_a5a39aab_14_carry_out_a019e228), .Result(Result[22]),
    .Carry_out_a019e228(full_adder_a5a39aab_15_carry_out_a019e228));
  Full_Adder_a5a39aab full_adder_a5a39aab_16 (
    .A(A[23]), .B(B[23]), .Carry_In_17b5218c(full_adder_a5a39aab_15_carry_out_a019e228), .Result(Result[23]),
    .Carry_out_a019e228(full_adder_a5a39aab_16_carry_out_a019e228));
  Full_Adder_a5a39aab full_adder_a5a39aab_17 (
    .A(A[8]), .B(B[8]), .Carry_In_17b5218c(full_adder_a5a39aab_16_carry_out_a019e228), .Result(Result[8]),
    .Carry_out_a019e228(full_adder_a5a39aab_17_carry_out_a019e228));
  Full_Adder_a5a39aab full_adder_a5a39aab_18 (
    .A(A[9]), .B(B[9]), .Carry_In_17b5218c(full_adder_a5a39aab_17_carry_out_a019e228), .Result(Result[9]),
    .Carry_out_a019e228(full_adder_a5a39aab_18_carry_out_a019e228));
  Full_Adder_a5a39aab full_adder_a5a39aab_19 (
    .A(A[10]), .B(B[10]), .Carry_In_17b5218c(full_adder_a5a39aab_18_carry_out_a019e228), .Result(Result[10]),
    .Carry_out_a019e228(full_adder_a5a39aab_19_carry_out_a019e228));
  Full_Adder_a5a39aab full_adder_a5a39aab_20 (
    .A(A[11]), .B(B[11]), .Carry_In_17b5218c(full_adder_a5a39aab_19_carry_out_a019e228), .Result(Result[11]),
    .Carry_out_a019e228(full_adder_a5a39aab_20_carry_out_a019e228));
  Full_Adder_a5a39aab full_adder_a5a39aab_21 (
    .A(A[12]), .B(B[12]), .Carry_In_17b5218c(full_adder_a5a39aab_20_carry_out_a019e228), .Result(Result[12]),
    .Carry_out_a019e228(full_adder_a5a39aab_21_carry_out_a019e228));
  Full_Adder_a5a39aab full_adder_a5a39aab_22 (
    .A(A[13]), .B(B[13]), .Carry_In_17b5218c(full_adder_a5a39aab_21_carry_out_a019e228), .Result(Result[13]),
    .Carry_out_a019e228(full_adder_a5a39aab_22_carry_out_a019e228));
  Full_Adder_a5a39aab full_adder_a5a39aab_23 (
    .A(A[14]), .B(B[14]), .Carry_In_17b5218c(full_adder_a5a39aab_22_carry_out_a019e228), .Result(Result[14]),
    .Carry_out_a019e228(full_adder_a5a39aab_23_carry_out_a019e228));
  Full_Adder_a5a39aab full_adder_a5a39aab_24 (
    .A(A[15]), .B(B[15]), .Carry_In_17b5218c(full_adder_a5a39aab_23_carry_out_a019e228), .Result(Result[15]),
    .Carry_out_a019e228(full_adder_a5a39aab_24_carry_out_a019e228));
  Full_Adder_a5a39aab full_adder_a5a39aab_25 (
    .A(A[0]), .B(B[0]), .Carry_In_17b5218c(full_adder_a5a39aab_24_carry_out_a019e228), .Result(Result[0]),
    .Carry_out_a019e228(full_adder_a5a39aab_25_carry_out_a019e228));
  Full_Adder_a5a39aab full_adder_a5a39aab_26 (
    .A(A[1]), .B(B[1]), .Carry_In_17b5218c(full_adder_a5a39aab_25_carry_out_a019e228), .Result(Result[1]),
    .Carry_out_a019e228(full_adder_a5a39aab_26_carry_out_a019e228));
  Full_Adder_a5a39aab full_adder_a5a39aab_27 (
    .A(A[2]), .B(B[2]), .Carry_In_17b5218c(full_adder_a5a39aab_26_carry_out_a019e228), .Result(Result[2]),
    .Carry_out_a019e228(full_adder_a5a39aab_27_carry_out_a019e228));
  Full_Adder_a5a39aab full_adder_a5a39aab_28 (
    .A(A[3]), .B(B[3]), .Carry_In_17b5218c(full_adder_a5a39aab_27_carry_out_a019e228), .Result(Result[3]),
    .Carry_out_a019e228(full_adder_a5a39aab_28_carry_out_a019e228));
  Full_Adder_a5a39aab full_adder_a5a39aab_29 (
    .A(A[4]), .B(B[4]), .Carry_In_17b5218c(full_adder_a5a39aab_28_carry_out_a019e228), .Result(Result[4]),
    .Carry_out_a019e228(full_adder_a5a39aab_29_carry_out_a019e228));
  Full_Adder_a5a39aab full_adder_a5a39aab_30 (
    .A(A[5]), .B(B[5]), .Carry_In_17b5218c(full_adder_a5a39aab_29_carry_out_a019e228), .Result(Result[5]),
    .Carry_out_a019e228(full_adder_a5a39aab_30_carry_out_a019e228));
  Full_Adder_a5a39aab full_adder_a5a39aab_31 (
    .A(A[6]), .B(B[6]), .Carry_In_17b5218c(full_adder_a5a39aab_30_carry_out_a019e228), .Result(Result[6]),
    .Carry_out_a019e228(full_adder_a5a39aab_31_carry_out_a019e228));
  Full_Adder_a5a39aab full_adder_a5a39aab_32 (
    .A(A[7]), .B(B[7]), .Carry_In_17b5218c(full_adder_a5a39aab_31_carry_out_a019e228), .Result(Result[7]));  // open: Carry_out_a019e228
endmodule

module L_32_bit_AND_28c7e6f7 (
  input  [31:0] A,
  input  [31:0] B,
  output [31:0] Result
);

  and and_1 (Result[24], A[24], B[24]);
  and and_2 (Result[25], A[25], B[25]);
  and and_3 (Result[26], A[26], B[26]);
  and and_4 (Result[27], A[27], B[27]);
  and and_5 (Result[28], A[28], B[28]);
  and and_6 (Result[29], A[29], B[29]);
  and and_7 (Result[30], A[30], B[30]);
  and and_8 (Result[31], A[31], B[31]);
  and and_9 (Result[16], A[16], B[16]);
  and and_10 (Result[17], A[17], B[17]);
  and and_11 (Result[18], A[18], B[18]);
  and and_12 (Result[19], A[19], B[19]);
  and and_13 (Result[20], A[20], B[20]);
  and and_14 (Result[21], A[21], B[21]);
  and and_15 (Result[22], A[22], B[22]);
  and and_16 (Result[23], A[23], B[23]);
  and and_17 (Result[8], A[8], B[8]);
  and and_18 (Result[9], A[9], B[9]);
  and and_19 (Result[10], A[10], B[10]);
  and and_20 (Result[11], A[11], B[11]);
  and and_21 (Result[12], A[12], B[12]);
  and and_22 (Result[13], A[13], B[13]);
  and and_23 (Result[14], A[14], B[14]);
  and and_24 (Result[15], A[15], B[15]);
  and and_25 (Result[0], A[0], B[0]);
  and and_26 (Result[1], A[1], B[1]);
  and and_27 (Result[2], A[2], B[2]);
  and and_28 (Result[3], A[3], B[3]);
  and and_29 (Result[4], A[4], B[4]);
  and and_30 (Result[5], A[5], B[5]);
  and and_31 (Result[6], A[6], B[6]);
  and and_32 (Result[7], A[7], B[7]);
endmodule

module L_32_bit_OR_08d9d074 (
  input  [31:0] A,
  input  [31:0] B,
  output [31:0] Result
);

  or or_1 (Result[24], A[24], B[24]);
  or or_2 (Result[25], A[25], B[25]);
  or or_3 (Result[26], A[26], B[26]);
  or or_4 (Result[27], A[27], B[27]);
  or or_5 (Result[28], A[28], B[28]);
  or or_6 (Result[29], A[29], B[29]);
  or or_7 (Result[30], A[30], B[30]);
  or or_8 (Result[31], A[31], B[31]);
  or or_9 (Result[16], A[16], B[16]);
  or or_10 (Result[17], A[17], B[17]);
  or or_11 (Result[18], A[18], B[18]);
  or or_12 (Result[19], A[19], B[19]);
  or or_13 (Result[20], A[20], B[20]);
  or or_14 (Result[21], A[21], B[21]);
  or or_15 (Result[22], A[22], B[22]);
  or or_16 (Result[23], A[23], B[23]);
  or or_17 (Result[8], A[8], B[8]);
  or or_18 (Result[9], A[9], B[9]);
  or or_19 (Result[10], A[10], B[10]);
  or or_20 (Result[11], A[11], B[11]);
  or or_21 (Result[12], A[12], B[12]);
  or or_22 (Result[13], A[13], B[13]);
  or or_23 (Result[14], A[14], B[14]);
  or or_24 (Result[15], A[15], B[15]);
  or or_25 (Result[0], A[0], B[0]);
  or or_26 (Result[1], A[1], B[1]);
  or or_27 (Result[2], A[2], B[2]);
  or or_28 (Result[3], A[3], B[3]);
  or or_29 (Result[4], A[4], B[4]);
  or or_30 (Result[5], A[5], B[5]);
  or or_31 (Result[6], A[6], B[6]);
  or or_32 (Result[7], A[7], B[7]);
endmodule

module L_32_bit_Subtractor_26bf78db (
  input  [31:0] B,
  input  [31:0] A,
  output OF,
  output Cout,
  output [31:0] S
);

  wire full_adder2_2d79c7a2_1_carry_out_a019e228, full_adder2_2d79c7a2_2_carry_out_a019e228,
       full_adder2_2d79c7a2_3_carry_out_a019e228, full_adder2_2d79c7a2_4_carry_out_a019e228,
       full_adder2_2d79c7a2_5_carry_out_a019e228, full_adder2_2d79c7a2_6_carry_out_a019e228,
       full_adder2_2d79c7a2_7_carry_out_a019e228, full_adder2_2d79c7a2_8_carry_out_a019e228,
       full_adder2_2d79c7a2_9_carry_out_a019e228, full_adder2_2d79c7a2_10_carry_out_a019e228,
       full_adder2_2d79c7a2_11_carry_out_a019e228, full_adder2_2d79c7a2_12_carry_out_a019e228,
       full_adder2_2d79c7a2_13_carry_out_a019e228, full_adder2_2d79c7a2_14_carry_out_a019e228,
       full_adder2_2d79c7a2_15_carry_out_a019e228, full_adder2_2d79c7a2_16_carry_out_a019e228,
       full_adder2_2d79c7a2_17_carry_out_a019e228, full_adder2_2d79c7a2_18_carry_out_a019e228,
       full_adder2_2d79c7a2_19_carry_out_a019e228, full_adder2_2d79c7a2_20_carry_out_a019e228,
       full_adder2_2d79c7a2_21_carry_out_a019e228, full_adder2_2d79c7a2_22_carry_out_a019e228,
       full_adder2_2d79c7a2_23_carry_out_a019e228, full_adder2_2d79c7a2_24_carry_out_a019e228,
       full_adder2_2d79c7a2_25_carry_out_a019e228, full_adder2_2d79c7a2_26_carry_out_a019e228,
       full_adder2_2d79c7a2_27_carry_out_a019e228, full_adder2_2d79c7a2_28_carry_out_a019e228,
       full_adder2_2d79c7a2_29_carry_out_a019e228, full_adder2_2d79c7a2_30_carry_out_a019e228,
       full_adder2_2d79c7a2_31_carry_out_a019e228, full_adder2_2d79c7a2_32_carry_out_a019e228, not_1_out,
       undriven, xor_3_out, xor_4_out, xor_5_out, xor_6_out, xor_7_out, xor_8_out, xor_9_out, xor_10_out,
       xor_11_out, xor_12_out, xor_13_out, xor_14_out, xor_15_out, xor_16_out, xor_17_out, xor_18_out,
       xor_19_out, xor_20_out, xor_21_out, xor_22_out, xor_23_out, xor_24_out, xor_25_out, xor_26_out,
       xor_27_out, xor_28_out, xor_29_out, xor_30_out, xor_31_out, xor_32_out, xor_33_out, xor_34_out,
       xor_35_out;

  xor xor_1 (OF, full_adder2_2d79c7a2_2_carry_out_a019e228, full_adder2_2d79c7a2_1_carry_out_a019e228);
  xor xor_2 (Cout, not_1_out, full_adder2_2d79c7a2_1_carry_out_a019e228);
  xor xor_3 (xor_3_out, B[31], not_1_out);
  Full_Adder2_2d79c7a2 full_adder2_2d79c7a2_1 (
    .A(xor_3_out), .B(A[31]), .Carry_In_17b5218c(full_adder2_2d79c7a2_2_carry_out_a019e228), .Result(S[31]),
    .Carry_out_a019e228(full_adder2_2d79c7a2_1_carry_out_a019e228));
  xor xor_4 (xor_4_out, B[30], not_1_out);
  Full_Adder2_2d79c7a2 full_adder2_2d79c7a2_2 (
    .A(xor_4_out), .B(A[30]), .Carry_In_17b5218c(full_adder2_2d79c7a2_3_carry_out_a019e228), .Result(S[30]),
    .Carry_out_a019e228(full_adder2_2d79c7a2_2_carry_out_a019e228));
  xor xor_5 (xor_5_out, B[29], not_1_out);
  Full_Adder2_2d79c7a2 full_adder2_2d79c7a2_3 (
    .A(xor_5_out), .B(A[29]), .Carry_In_17b5218c(full_adder2_2d79c7a2_4_carry_out_a019e228), .Result(S[29]),
    .Carry_out_a019e228(full_adder2_2d79c7a2_3_carry_out_a019e228));
  xor xor_6 (xor_6_out, B[28], not_1_out);
  Full_Adder2_2d79c7a2 full_adder2_2d79c7a2_4 (
    .A(xor_6_out), .B(A[28]), .Carry_In_17b5218c(full_adder2_2d79c7a2_5_carry_out_a019e228), .Result(S[28]),
    .Carry_out_a019e228(full_adder2_2d79c7a2_4_carry_out_a019e228));
  xor xor_7 (xor_7_out, B[27], not_1_out);
  Full_Adder2_2d79c7a2 full_adder2_2d79c7a2_5 (
    .A(xor_7_out), .B(A[27]), .Carry_In_17b5218c(full_adder2_2d79c7a2_6_carry_out_a019e228), .Result(S[27]),
    .Carry_out_a019e228(full_adder2_2d79c7a2_5_carry_out_a019e228));
  xor xor_8 (xor_8_out, B[26], not_1_out);
  Full_Adder2_2d79c7a2 full_adder2_2d79c7a2_6 (
    .A(xor_8_out), .B(A[26]), .Carry_In_17b5218c(full_adder2_2d79c7a2_7_carry_out_a019e228), .Result(S[26]),
    .Carry_out_a019e228(full_adder2_2d79c7a2_6_carry_out_a019e228));
  xor xor_9 (xor_9_out, B[25], not_1_out);
  Full_Adder2_2d79c7a2 full_adder2_2d79c7a2_7 (
    .A(xor_9_out), .B(A[25]), .Carry_In_17b5218c(full_adder2_2d79c7a2_8_carry_out_a019e228), .Result(S[25]),
    .Carry_out_a019e228(full_adder2_2d79c7a2_7_carry_out_a019e228));
  xor xor_10 (xor_10_out, B[24], not_1_out);
  Full_Adder2_2d79c7a2 full_adder2_2d79c7a2_8 (
    .A(xor_10_out), .B(A[24]), .Carry_In_17b5218c(full_adder2_2d79c7a2_9_carry_out_a019e228), .Result(S[24]),
    .Carry_out_a019e228(full_adder2_2d79c7a2_8_carry_out_a019e228));
  xor xor_11 (xor_11_out, B[23], not_1_out);
  Full_Adder2_2d79c7a2 full_adder2_2d79c7a2_9 (
    .A(xor_11_out), .B(A[23]), .Carry_In_17b5218c(full_adder2_2d79c7a2_10_carry_out_a019e228),
    .Result(S[23]), .Carry_out_a019e228(full_adder2_2d79c7a2_9_carry_out_a019e228));
  xor xor_12 (xor_12_out, B[22], not_1_out);
  Full_Adder2_2d79c7a2 full_adder2_2d79c7a2_10 (
    .A(xor_12_out), .B(A[22]), .Carry_In_17b5218c(full_adder2_2d79c7a2_11_carry_out_a019e228),
    .Result(S[22]), .Carry_out_a019e228(full_adder2_2d79c7a2_10_carry_out_a019e228));
  xor xor_13 (xor_13_out, B[21], not_1_out);
  Full_Adder2_2d79c7a2 full_adder2_2d79c7a2_11 (
    .A(xor_13_out), .B(A[21]), .Carry_In_17b5218c(full_adder2_2d79c7a2_12_carry_out_a019e228),
    .Result(S[21]), .Carry_out_a019e228(full_adder2_2d79c7a2_11_carry_out_a019e228));
  xor xor_14 (xor_14_out, B[20], not_1_out);
  Full_Adder2_2d79c7a2 full_adder2_2d79c7a2_12 (
    .A(xor_14_out), .B(A[20]), .Carry_In_17b5218c(full_adder2_2d79c7a2_13_carry_out_a019e228),
    .Result(S[20]), .Carry_out_a019e228(full_adder2_2d79c7a2_12_carry_out_a019e228));
  xor xor_15 (xor_15_out, B[19], not_1_out);
  Full_Adder2_2d79c7a2 full_adder2_2d79c7a2_13 (
    .A(xor_15_out), .B(A[19]), .Carry_In_17b5218c(full_adder2_2d79c7a2_14_carry_out_a019e228),
    .Result(S[19]), .Carry_out_a019e228(full_adder2_2d79c7a2_13_carry_out_a019e228));
  xor xor_16 (xor_16_out, B[18], not_1_out);
  Full_Adder2_2d79c7a2 full_adder2_2d79c7a2_14 (
    .A(xor_16_out), .B(A[18]), .Carry_In_17b5218c(full_adder2_2d79c7a2_15_carry_out_a019e228),
    .Result(S[18]), .Carry_out_a019e228(full_adder2_2d79c7a2_14_carry_out_a019e228));
  xor xor_17 (xor_17_out, B[17], not_1_out);
  Full_Adder2_2d79c7a2 full_adder2_2d79c7a2_15 (
    .A(xor_17_out), .B(A[17]), .Carry_In_17b5218c(full_adder2_2d79c7a2_16_carry_out_a019e228),
    .Result(S[17]), .Carry_out_a019e228(full_adder2_2d79c7a2_15_carry_out_a019e228));
  xor xor_18 (xor_18_out, B[16], not_1_out);
  Full_Adder2_2d79c7a2 full_adder2_2d79c7a2_16 (
    .A(xor_18_out), .B(A[16]), .Carry_In_17b5218c(full_adder2_2d79c7a2_17_carry_out_a019e228),
    .Result(S[16]), .Carry_out_a019e228(full_adder2_2d79c7a2_16_carry_out_a019e228));
  xor xor_19 (xor_19_out, B[15], not_1_out);
  Full_Adder2_2d79c7a2 full_adder2_2d79c7a2_17 (
    .A(xor_19_out), .B(A[15]), .Carry_In_17b5218c(full_adder2_2d79c7a2_18_carry_out_a019e228),
    .Result(S[15]), .Carry_out_a019e228(full_adder2_2d79c7a2_17_carry_out_a019e228));
  xor xor_20 (xor_20_out, B[14], not_1_out);
  Full_Adder2_2d79c7a2 full_adder2_2d79c7a2_18 (
    .A(xor_20_out), .B(A[14]), .Carry_In_17b5218c(full_adder2_2d79c7a2_19_carry_out_a019e228),
    .Result(S[14]), .Carry_out_a019e228(full_adder2_2d79c7a2_18_carry_out_a019e228));
  xor xor_21 (xor_21_out, B[13], not_1_out);
  Full_Adder2_2d79c7a2 full_adder2_2d79c7a2_19 (
    .A(xor_21_out), .B(A[13]), .Carry_In_17b5218c(full_adder2_2d79c7a2_20_carry_out_a019e228),
    .Result(S[13]), .Carry_out_a019e228(full_adder2_2d79c7a2_19_carry_out_a019e228));
  xor xor_22 (xor_22_out, B[12], not_1_out);
  Full_Adder2_2d79c7a2 full_adder2_2d79c7a2_20 (
    .A(xor_22_out), .B(A[12]), .Carry_In_17b5218c(full_adder2_2d79c7a2_21_carry_out_a019e228),
    .Result(S[12]), .Carry_out_a019e228(full_adder2_2d79c7a2_20_carry_out_a019e228));
  xor xor_23 (xor_23_out, B[11], not_1_out);
  Full_Adder2_2d79c7a2 full_adder2_2d79c7a2_21 (
    .A(xor_23_out), .B(A[11]), .Carry_In_17b5218c(full_adder2_2d79c7a2_22_carry_out_a019e228),
    .Result(S[11]), .Carry_out_a019e228(full_adder2_2d79c7a2_21_carry_out_a019e228));
  xor xor_24 (xor_24_out, B[10], not_1_out);
  Full_Adder2_2d79c7a2 full_adder2_2d79c7a2_22 (
    .A(xor_24_out), .B(A[10]), .Carry_In_17b5218c(full_adder2_2d79c7a2_23_carry_out_a019e228),
    .Result(S[10]), .Carry_out_a019e228(full_adder2_2d79c7a2_22_carry_out_a019e228));
  xor xor_25 (xor_25_out, B[9], not_1_out);
  Full_Adder2_2d79c7a2 full_adder2_2d79c7a2_23 (
    .A(xor_25_out), .B(A[9]), .Carry_In_17b5218c(full_adder2_2d79c7a2_24_carry_out_a019e228), .Result(S[9]),
    .Carry_out_a019e228(full_adder2_2d79c7a2_23_carry_out_a019e228));
  xor xor_26 (xor_26_out, B[8], not_1_out);
  Full_Adder2_2d79c7a2 full_adder2_2d79c7a2_24 (
    .A(xor_26_out), .B(A[8]), .Carry_In_17b5218c(full_adder2_2d79c7a2_25_carry_out_a019e228), .Result(S[8]),
    .Carry_out_a019e228(full_adder2_2d79c7a2_24_carry_out_a019e228));
  xor xor_27 (xor_27_out, B[7], not_1_out);
  Full_Adder2_2d79c7a2 full_adder2_2d79c7a2_25 (
    .A(xor_27_out), .B(A[7]), .Carry_In_17b5218c(full_adder2_2d79c7a2_26_carry_out_a019e228), .Result(S[7]),
    .Carry_out_a019e228(full_adder2_2d79c7a2_25_carry_out_a019e228));
  xor xor_28 (xor_28_out, B[6], not_1_out);
  Full_Adder2_2d79c7a2 full_adder2_2d79c7a2_26 (
    .A(xor_28_out), .B(A[6]), .Carry_In_17b5218c(full_adder2_2d79c7a2_27_carry_out_a019e228), .Result(S[6]),
    .Carry_out_a019e228(full_adder2_2d79c7a2_26_carry_out_a019e228));
  xor xor_29 (xor_29_out, B[5], not_1_out);
  Full_Adder2_2d79c7a2 full_adder2_2d79c7a2_27 (
    .A(xor_29_out), .B(A[5]), .Carry_In_17b5218c(full_adder2_2d79c7a2_28_carry_out_a019e228), .Result(S[5]),
    .Carry_out_a019e228(full_adder2_2d79c7a2_27_carry_out_a019e228));
  xor xor_30 (xor_30_out, B[4], not_1_out);
  Full_Adder2_2d79c7a2 full_adder2_2d79c7a2_28 (
    .A(xor_30_out), .B(A[4]), .Carry_In_17b5218c(full_adder2_2d79c7a2_29_carry_out_a019e228), .Result(S[4]),
    .Carry_out_a019e228(full_adder2_2d79c7a2_28_carry_out_a019e228));
  xor xor_31 (xor_31_out, B[3], not_1_out);
  Full_Adder2_2d79c7a2 full_adder2_2d79c7a2_29 (
    .A(xor_31_out), .B(A[3]), .Carry_In_17b5218c(full_adder2_2d79c7a2_30_carry_out_a019e228), .Result(S[3]),
    .Carry_out_a019e228(full_adder2_2d79c7a2_29_carry_out_a019e228));
  xor xor_32 (xor_32_out, B[2], not_1_out);
  Full_Adder2_2d79c7a2 full_adder2_2d79c7a2_30 (
    .A(xor_32_out), .B(A[2]), .Carry_In_17b5218c(full_adder2_2d79c7a2_31_carry_out_a019e228), .Result(S[2]),
    .Carry_out_a019e228(full_adder2_2d79c7a2_30_carry_out_a019e228));
  xor xor_33 (xor_33_out, B[1], not_1_out);
  Full_Adder2_2d79c7a2 full_adder2_2d79c7a2_31 (
    .A(xor_33_out), .B(A[1]), .Carry_In_17b5218c(full_adder2_2d79c7a2_32_carry_out_a019e228), .Result(S[1]),
    .Carry_out_a019e228(full_adder2_2d79c7a2_31_carry_out_a019e228));
  ExactlyOne xor_34 (.out(xor_34_out), .in1(B[0]), .in3(not_1_out), .in4(undriven));
  Full_Adder2_2d79c7a2 full_adder2_2d79c7a2_32 (
    .A(xor_34_out), .B(A[0]), .Carry_In_17b5218c(xor_35_out), .Result(S[0]),
    .Carry_out_a019e228(full_adder2_2d79c7a2_32_carry_out_a019e228));
  ExactlyOne xor_35 (.out(xor_35_out), .in0(undriven), .in1(1'b0), .in3(not_1_out));
  not not_1 (not_1_out, 1'b0);
endmodule

module Full_Adder_a5a39aab (
  input  Carry_In_17b5218c,
  input  A,
  input  B,
  output Result,
  output Carry_out_a019e228
);

  wire and_1_out, and_2_out, xor_1_out;

  xor xor_1 (xor_1_out, A, B);
  and and_1 (and_1_out, B, A);
  and and_2 (and_2_out, xor_1_out, Carry_In_17b5218c);
  xor xor_2 (Result, Carry_In_17b5218c, xor_1_out);
  or or_1 (Carry_out_a019e228, and_2_out, and_1_out);
endmodule

module Full_Adder2_2d79c7a2 (
  input  Carry_In_17b5218c,
  input  A,
  input  B,
  output Result,
  output Carry_out_a019e228
);

  wire and_1_out, and_2_out, xor_1_out;

  xor xor_1 (xor_1_out, A, B);
  and and_1 (and_1_out, B, A);
  xor xor_2 (Result, xor_1_out, Carry_In_17b5218c);
  and and_2 (and_2_out, xor_1_out, Carry_In_17b5218c);
  or or_1 (Carry_out_a019e228, and_2_out, and_1_out);
endmodule

module NOT_32_bit_929ae11d (
  input  [31:0] A,
  output [31:0] NotA
);

  not not_1 (NotA[0], A[0]);
  not not_2 (NotA[1], A[1]);
  not not_3 (NotA[2], A[2]);
  not not_4 (NotA[3], A[3]);
  not not_5 (NotA[4], A[4]);
  not not_6 (NotA[5], A[5]);
  not not_7 (NotA[6], A[6]);
  not not_8 (NotA[7], A[7]);
  not not_9 (NotA[8], A[8]);
  not not_10 (NotA[9], A[9]);
  not not_11 (NotA[10], A[10]);
  not not_12 (NotA[11], A[11]);
  not not_13 (NotA[12], A[12]);
  not not_14 (NotA[13], A[13]);
  not not_15 (NotA[14], A[14]);
  not not_16 (NotA[15], A[15]);
  not not_17 (NotA[16], A[16]);
  not not_18 (NotA[17], A[17]);
  not not_19 (NotA[18], A[18]);
  not not_20 (NotA[19], A[19]);
  not not_21 (NotA[20], A[20]);
  not not_22 (NotA[21], A[21]);
  not not_23 (NotA[22], A[22]);
  not not_24 (NotA[23], A[23]);
  not not_25 (NotA[24], A[24]);
  not not_26 (NotA[25], A[25]);
  not not_27 (NotA[26], A[26]);
  not not_28 (NotA[27], A[27]);
  not not_29 (NotA[28], A[28]);
  not not_30 (NotA[29], A[29]);
  not not_31 (NotA[30], A[30]);
  not not_32 (NotA[31], A[31]);
endmodule

module Two_s_Complement_32_bit_72d07b45 (
  input  [31:0] A,
  output [31:0] TwosompA
);

  wire [31:0] not_32_bit_929ae11d_1_nota;

  NOT_32_bit_929ae11d not_32_bit_929ae11d_1 (.A(A), .NotA(not_32_bit_929ae11d_1_nota));
  L_32_bit_Adder_cc387356 l_32_bit_adder_cc387356_1 (.A(not_32_bit_929ae11d_1_nota), .B({32{1'b0}}), .Result(TwosompA));
endmodule

module L_32_bit_multiplier_6d85dbff (
  input  [31:0] M,
  input  [31:0] Q,
  input  Init,
  output out_4,
  output out_5,
  output [31:0] MSB,
  output [31:0] LSB
);

  wire and_2_out, Clk_out, counter_1_carry, not_2_out, not_3_out, shift_register_1_out, shift_register_2_out,
       shift_register_3_q0, xnor_1_out;
  wire [31:0] multiplexer_3_out, shift_register_1_q31, shift_register_2_q31, subtractor_1_out;

  Clock Clk (.out(Clk_out));
  not not_1 (out_5, counter_1_carry);
  and and_1 (out_4, Clk_out, out_5);
  not not_2 (not_2_out, out_4);
  Counter #(.width(6), .max('h3f), .ongoal("stay")) counter_1 (
    .carry(counter_1_carry), .clk(out_4));  // open: load, D, count, Q, clr
  Shift_Register #(.length(32)) shift_register_1 (
    .shift(not_2_out), .in(shift_register_1_q31[31]), .clk(out_4), .out(shift_register_1_out), .load(out_4),
    .d0(multiplexer_3_out[31]), .q0(shift_register_1_q31[31]), .d1(multiplexer_3_out[30]),
    .q1(shift_register_1_q31[30]), .d2(multiplexer_3_out[29]), .q2(shift_register_1_q31[29]),
    .d3(multiplexer_3_out[28]), .q3(shift_register_1_q31[28]), .d4(multiplexer_3_out[27]),
    .q4(shift_register_1_q31[27]), .d5(multiplexer_3_out[26]), .q5(shift_register_1_q31[26]),
    .d6(multiplexer_3_out[25]), .q6(shift_register_1_q31[25]), .d7(multiplexer_3_out[24]),
    .q7(shift_register_1_q31[24]), .d8(multiplexer_3_out[23]), .q8(shift_register_1_q31[23]),
    .d9(multiplexer_3_out[22]), .q9(shift_register_1_q31[22]), .d10(multiplexer_3_out[21]),
    .q10(shift_register_1_q31[21]), .d11(multiplexer_3_out[20]), .q11(shift_register_1_q31[20]),
    .d12(multiplexer_3_out[19]), .q12(shift_register_1_q31[19]), .d13(multiplexer_3_out[18]),
    .q13(shift_register_1_q31[18]), .d14(multiplexer_3_out[17]), .q14(shift_register_1_q31[17]),
    .d15(multiplexer_3_out[16]), .q15(shift_register_1_q31[16]), .d16(multiplexer_3_out[15]),
    .q16(shift_register_1_q31[15]), .d17(multiplexer_3_out[14]), .q17(shift_register_1_q31[14]),
    .d18(multiplexer_3_out[13]), .q18(shift_register_1_q31[13]), .d19(multiplexer_3_out[12]),
    .q19(shift_register_1_q31[12]), .d20(multiplexer_3_out[11]), .q20(shift_register_1_q31[11]),
    .d21(multiplexer_3_out[10]), .q21(shift_register_1_q31[10]), .d22(multiplexer_3_out[9]),
    .q22(shift_register_1_q31[9]), .d23(multiplexer_3_out[8]), .q23(shift_register_1_q31[8]),
    .d24(multiplexer_3_out[7]), .q24(shift_register_1_q31[7]), .d25(multiplexer_3_out[6]),
    .q25(shift_register_1_q31[6]), .d26(multiplexer_3_out[5]), .q26(shift_register_1_q31[5]),
    .d27(multiplexer_3_out[4]), .q27(shift_register_1_q31[4]), .d28(multiplexer_3_out[3]),
    .q28(shift_register_1_q31[3]), .d29(multiplexer_3_out[2]), .q29(shift_register_1_q31[2]),
    .d30(multiplexer_3_out[1]), .q30(shift_register_1_q31[1]), .d31(multiplexer_3_out[0]),
    .q31(shift_register_1_q31[0]));  // open: clr
  Multiplexer #(.width(32)) multiplexer_1 (
    .in0({32{1'b0}}), .in1(shift_register_1_q31), .out(MSB), .sel(counter_1_carry));  // open: en
  Multiplexer #(.width(32)) multiplexer_2 (
    .in0({32{1'b0}}), .in1(shift_register_2_q31), .out(LSB), .sel(counter_1_carry));  // open: en
  Shift_Register #(.length(32)) shift_register_2 (
    .shift(not_2_out), .in(shift_register_1_out), .clk(out_4), .out(shift_register_2_out), .load(Init),
    .d0(Q[31]), .q0(shift_register_2_q31[31]), .d1(Q[30]), .q1(shift_register_2_q31[30]), .d2(Q[29]),
    .q2(shift_register_2_q31[29]), .d3(Q[28]), .q3(shift_register_2_q31[28]), .d4(Q[27]),
    .q4(shift_register_2_q31[27]), .d5(Q[26]), .q5(shift_register_2_q31[26]), .d6(Q[25]),
    .q6(shift_register_2_q31[25]), .d7(Q[24]), .q7(shift_register_2_q31[24]), .d8(Q[23]),
    .q8(shift_register_2_q31[23]), .d9(Q[22]), .q9(shift_register_2_q31[22]), .d10(Q[21]),
    .q10(shift_register_2_q31[21]), .d11(Q[20]), .q11(shift_register_2_q31[20]), .d12(Q[19]),
    .q12(shift_register_2_q31[19]), .d13(Q[18]), .q13(shift_register_2_q31[18]), .d14(Q[17]),
    .q14(shift_register_2_q31[17]), .d15(Q[16]), .q15(shift_register_2_q31[16]), .d16(Q[15]),
    .q16(shift_register_2_q31[15]), .d17(Q[14]), .q17(shift_register_2_q31[14]), .d18(Q[13]),
    .q18(shift_register_2_q31[13]), .d19(Q[12]), .q19(shift_register_2_q31[12]), .d20(Q[11]),
    .q20(shift_register_2_q31[11]), .d21(Q[10]), .q21(shift_register_2_q31[10]), .d22(Q[9]),
    .q22(shift_register_2_q31[9]), .d23(Q[8]), .q23(shift_register_2_q31[8]), .d24(Q[7]),
    .q24(shift_register_2_q31[7]), .d25(Q[6]), .q25(shift_register_2_q31[6]), .d26(Q[5]),
    .q26(shift_register_2_q31[5]), .d27(Q[4]), .q27(shift_register_2_q31[4]), .d28(Q[3]),
    .q28(shift_register_2_q31[3]), .d29(Q[2]), .q29(shift_register_2_q31[2]), .d30(Q[1]),
    .q30(shift_register_2_q31[1]), .d31(Q[0]), .q31(shift_register_2_q31[0]));  // open: clr
  Multiplexer #(.width(32)) multiplexer_3 (
    .in0(subtractor_1_out), .in1(shift_register_1_q31), .out(multiplexer_3_out), .sel(xnor_1_out));  // open: en
  xnor xnor_1 (xnor_1_out, shift_register_2_q31[0], shift_register_3_q0);
  and and_2 (and_2_out, shift_register_2_q31[0], not_3_out);
  not not_3 (not_3_out, shift_register_3_q0);
  Subtractor #(.width(32)) subtractor_1 (
    .a(shift_register_1_q31), .b(M), .out(subtractor_1_out), .bin(and_2_out));  // open: bout
  Shift_Register #(.length(1)) shift_register_3 (
    .shift(not_2_out), .in(shift_register_2_out), .clk(out_4), .q0(shift_register_3_q0));  // open: out, load, clr, d0
endmodule

module L_4_bit_booth_multiplier_b75a9ba5 (
  input  [3:0] M,
  input  [3:0] Q,
  input  Init,
  input  Shift,
  input  Load
);

  wire clock_1_out, shift_register_1_out, shift_register_2_out, shift_register_2_q3, shift_register_3_q0;
  wire [2:0] comparator_1_gt;
  wire [3:0] adder_1_out, multiplexer_1_out, shift_register_1_q3, subtractor_1_out;

  Multiplexer #(.select(3), .width(4)) multiplexer_1 (
    .in1(subtractor_1_out), .in2(shift_register_1_q3), .in4(adder_1_out), .out(multiplexer_1_out),
    .sel(comparator_1_gt));  // open: in0, in3, in5, in6, in7, en
  Clock clock_1 (.out(clock_1_out));
  Shift_Register #(.length(4)) shift_register_1 (
    .shift(Shift), .in(shift_register_1_q3[3]), .clk(clock_1_out), .out(shift_register_1_out), .load(Load),
    .d0(multiplexer_1_out[3]), .q0(shift_register_1_q3[3]), .d1(multiplexer_1_out[2]),
    .q1(shift_register_1_q3[2]), .d2(multiplexer_1_out[1]), .q2(shift_register_1_q3[1]),
    .d3(multiplexer_1_out[0]), .q3(shift_register_1_q3[0]));  // open: clr
  Shift_Register #(.length(4)) shift_register_2 (
    .shift(Shift), .in(shift_register_1_out), .clk(clock_1_out), .out(shift_register_2_out), .load(Init),
    .d0(Q[3]), .d1(Q[2]), .d2(Q[1]), .d3(Q[0]), .q3(shift_register_2_q3));  // open: clr, q0, q1, q2
  Subtractor #(.width(4)) subtractor_1 (
    .a(shift_register_1_q3), .b(M), .out(subtractor_1_out), .bin(1'b0));  // open: bout
  Adder #(.width(4)) adder_1 (.a(shift_register_1_q3), .b(M), .out(adder_1_out), .cin(1'b0));  // open: cout
  Shift_Register #(.length(1)) shift_register_3 (
    .shift(Shift), .in(shift_register_2_out), .clk(clock_1_out), .q0(shift_register_3_q0));  // open: out, load, clr, d0
  Comparator #(.width(1)) comparator_1 (
    .a(shift_register_3_q0), .b(shift_register_2_q3), .gt(comparator_1_gt[0]), .eq(comparator_1_gt[1]),
    .lt(comparator_1_gt[2]));
endmodule
